// Logisim project BigASM.circ as structural Verilog
module BOARD_BIG_ASM (
  output out_1
);

  wire button_1_out, CLK, CLR, d_ff_1_q, not_1_out, Write, Write_ASCII;
  wire [6:0] ASCII;
  wire [7:0] counter_1_q;
  wire [23:0] Dir_INPUT, Dir_MEMORY;
  wire [31:0] INPUT, MEMORY_IN, MEMORY_OUT;

  Button button_1 (.out(button_1_out));
  Clock clock_1 (.out(CLK));
  D_Flip_Flop d_ff_1 (.clk(CLK), .D(1'b1), .Q(d_ff_1_q), .reset(button_1_out));  // open: Qn, preset, en
  D_Flip_Flop d_ff_2 (.clk(CLK), .D(d_ff_1_q), .Qn(CLR), .reset(button_1_out));  // open: Q, preset, en
  BIG_ASM big_asm_1 (
    .DATA_INPUT(INPUT), .MEMORY_IN(MEMORY_OUT), .CLK(CLK), .CLR(CLR), .DIR_INPUT(Dir_INPUT),
    .MEMORY_OUT(MEMORY_IN), .DIR_MEMORY(Dir_MEMORY), .Write_OUTPUT(Write), .ASCII(ASCII),
    .Write_ASCII(Write_ASCII), .END(out_1));
  MEMORY memory_1 (.DIR(Dir_MEMORY), .DATA_IN(MEMORY_IN), .WRITE(Write), .CLK(CLK), .CLR(CLR), .DATA_OUT(MEMORY_OUT));
  INPUT input_1 (.DIR(Dir_INPUT), .CLK(CLK), .DATA_OUT(INPUT));
  Counter counter_1 (.load(1'b0), .count(not_1_out), .Q(counter_1_q), .clk(CLK), .clr(CLR));  // open: D, carry
  not not_1 (not_1_out, out_1);
  // Probe on INPUT
  // Probe on counter_1_q
  TTY #(.rows(32), .cols(60)) tty_1 (.data(ASCII), .clk(CLK), .we(Write_ASCII), .clr(CLR));

  // Other names for the same wires on the sheet: END = out_1

  // Notes on the sheet:
  //   COUNTER
  //   BOARD
endmodule

module INPUT (
  input  [23:0] DIR,
  input  CLK,
  output [31:0] DATA_OUT
);

  RAM #(.addrWidth(24), .dataWidth(32)) ram_1 (.addr(DIR), .data(DATA_OUT), .clk(CLK), .ld(1'b1));  // open: sel, clr
endmodule

module MEMORY (
  input  [23:0] DIR,
  input  [31:0] DATA_IN,
  input  WRITE,
  input  CLK,
  input  CLR,
  output [31:0] DATA_OUT
);

  wire not_1_out;

  not not_1 (not_1_out, WRITE);
  RAM #(.addrWidth(24), .dataWidth(32), .bus("separate")) ram_1 (
    .addr(DIR), .din(DATA_IN), .data(DATA_OUT), .clk(CLK), .ld(not_1_out), .clr(CLR));  // open: str, sel
endmodule

module BIG_ASM (
  input  [31:0] DATA_INPUT,
  input  [31:0] MEMORY_IN,
  input  CLK,
  input  CLR,
  output [23:0] DIR_INPUT,
  output [31:0] MEMORY_OUT,
  output [23:0] DIR_MEMORY,
  output Write_OUTPUT,
  output [6:0] ASCII,
  output Write_ASCII,
  output END
);

  wire d_ff_1_q, d_ff_2_q, d_ff_5_q, end_print, jump, print_dec_1_write_ascii, start, start_print, write;
  wire [6:0] caracter, print_dec_1_ascii;
  wire [31:0] number, \output ;

  D_Flip_Flop d_ff_1 (.clk(CLK), .D(1'b1), .Q(d_ff_1_q), .reset(CLR));  // open: Qn, preset, en
  D_Flip_Flop d_ff_2 (.clk(CLK), .D(1'b1), .Q(d_ff_2_q), .reset(write));  // open: Qn, preset, en
  D_Flip_Flop d_ff_3 (.clk(CLK), .D(d_ff_1_q), .Qn(start), .reset(CLR));  // open: Q, preset, en
  D_Flip_Flop d_ff_4 (.clk(CLK), .D(d_ff_2_q), .Qn(start_print), .reset(write));  // open: Q, preset, en
  D_Flip_Flop d_ff_5 (.clk(CLK), .D(start_print), .Q(d_ff_5_q), .reset(CLR));  // open: Qn, preset, en
  Register #(.width(32)) register_1 (.D(\output ), .en(write), .Q(number), .clk(CLK), .clr(CLR));
  // Probe on number
  // Probe on \output 
  Restar_Matrices restar_matrices_1 (
    .Data_In(DATA_INPUT), .Clock(CLK), .Clear(CLR), .Start(start), .Data_Out(\output ),
    .Dir_Input(DIR_INPUT), .Done(END), .Write(write), .Done_print(end_print), .Jump(jump));
  PRINT_DEC print_dec_1 (
    .num(number), .start(d_ff_5_q), .CLK(CLK), .RST(CLR), .ASCII(print_dec_1_ascii),
    .Write_ASCII(print_dec_1_write_ascii), .END(end_print));
  Multiplexer #(.width(7), .enable("false")) multiplexer_1 (
    .in0(7'b0100000), .in1(7'b0001010), .out(caracter), .sel(jump));
  Multiplexer #(.width(7), .enable("false")) multiplexer_2 (
    .in0(print_dec_1_ascii), .in1(caracter), .out(ASCII), .sel(end_print));
  or or_1 (Write_ASCII, print_dec_1_write_ascii, end_print);
  // Probe on ASCII
endmodule

module PRINT_UDEC (
  input  [31:0] num,
  input  start,
  input  CLK,
  input  RST,
  output [6:0] ASCII,
  output Write_ASCII,
  output \end 
);

  wire _0_c, _0_n, demultiplexer_1_out0, demultiplexer_2_out0, demultiplexer_2_out1, demultiplexer_3_out0,
       demultiplexer_3_out1, IDLE_2_q, IDLE_3_q, IDLE_4_q, IDLE_q, Lc, Lc_0, Ln, Ln_0, or_1_out;
  wire [23:0] bit_extender_1_out;
  wire [31:0] c, c___1, c___1_t, divider_1_rem, memory_1_data_out, multiplexer_1_out, multiplexer_2_out,
       multiplexer_3_out, n, n___10, n___10___48;

  Multiplexer #(.width(32), .enable("false")) multiplexer_1 (
    .in0(num), .in1(n___10), .out(multiplexer_1_out), .sel(Lc_0));
  Divider #(.width(32)) divider_1 (.a(n), .b(32'ha), .out(n___10), .rem(divider_1_rem));  // open: upper
  Adder #(.width(32)) adder_1 (.a(divider_1_rem), .b(32'h30), .out(n___10___48));  // open: cin, cout
  or or_1 (or_1_out, demultiplexer_1_out0, \end );
  Register #(.width(32)) u_n (.D(multiplexer_1_out), .en(Ln), .Q(n), .clk(CLK), .clr(RST));
  D_Flip_Flop IDLE (.clk(CLK), .D(or_1_out), .Q(IDLE_q), .preset(RST));  // open: Qn, en, reset
  Demultiplexer #(.enable("false")) demultiplexer_1 (
    .out0(demultiplexer_1_out0), .out1(Ln_0), .in(IDLE_q), .sel(start));
  or or_2 (Write_ASCII, demultiplexer_3_out0, demultiplexer_2_out1);
  Multiplexer #(.width(32), .enable("false")) multiplexer_2 (
    .in0(c___1), .in1(c___1_t), .out(multiplexer_2_out), .sel(Write_ASCII));
  Adder #(.width(32)) adder_2 (.a(c), .b(32'h1), .out(c___1));  // open: cin, cout
  Subtractor #(.width(32)) subtractor_1 (.a(c), .b(32'h1), .out(c___1_t));  // open: bin, bout
  D_Flip_Flop IDLE_2 (.clk(CLK), .D(Ln_0), .Q(IDLE_2_q), .reset(RST));  // open: Qn, preset, en
  Register #(.width(32)) u_c (.D(multiplexer_2_out), .en(Lc), .Q(c), .clk(CLK), .clr(RST));
  or or_3 (Lc_0, IDLE_2_q, demultiplexer_3_out1);
  Multiplexer #(.width(32), .enable("false")) multiplexer_3 (
    .in0(c), .in1(c___1_t), .out(multiplexer_3_out), .sel(Write_ASCII));
  Comparator #(.width(32), .mode("unsigned")) comparator_1 (.a({32{1'b0}}), .b(n), .lt(_0_n));  // open: gt, eq
  Comparator #(.width(32), .mode("unsigned")) comparator_2 (.a({32{1'b0}}), .b(c), .lt(_0_c));  // open: gt, eq
  D_Flip_Flop IDLE_3 (.clk(CLK), .D(Write_ASCII), .Q(IDLE_3_q), .reset(RST));  // open: Qn, preset, en
  Demultiplexer #(.enable("false")) demultiplexer_2 (
    .out0(demultiplexer_2_out0), .out1(demultiplexer_2_out1), .in(IDLE_3_q), .sel(_0_c));
  Bit_Extender #(.in_width(32), .out_width(24)) bit_extender_1 (.in(multiplexer_3_out), .out(bit_extender_1_out));
  D_Flip_Flop IDLE_4 (.clk(CLK), .D(Lc_0), .Q(IDLE_4_q), .reset(RST));  // open: Qn, preset, en
  or or_4 (Lc, Lc_0, Write_ASCII);
  or or_5 (Ln, Ln_0, Lc_0);
  Demultiplexer #(.enable("false")) demultiplexer_3 (
    .out0(demultiplexer_3_out0), .out1(demultiplexer_3_out1), .in(IDLE_4_q), .sel(_0_n));
  D_Flip_Flop IDLE_5 (.clk(CLK), .D(demultiplexer_2_out0), .Q(\end ), .reset(RST));  // open: Qn, preset, en
  MEMORY memory_1 (
    .DIR(bit_extender_1_out), .DATA_IN(n___10___48), .WRITE(Lc_0), .CLK(CLK), .CLR(RST),
    .DATA_OUT(memory_1_data_out));
  Bit_Extender #(.in_width(32), .out_width(7)) bit_extender_2 (.in(memory_1_data_out), .out(ASCII));

  // Other names for the same wires on the sheet: Lc_1 = Write_ASCII; Sc = Write_ASCII; Ln_1 = Lc_0; Sn = Lc_0;
  //   Write = Lc_0
endmodule

module PRINT_DEC (
  input  [31:0] num,
  input  start,
  input  CLK,
  input  RST,
  output [6:0] ASCII,
  output Write_ASCII,
  output END
);

  wire demultiplexer_1_out0, demultiplexer_1_out1, demultiplexer_2_out0, demultiplexer_3_out0, end_t,
       IDLE_3_q, IDLE_q, or_1_out, or_2_out, or_3_out, S_ASCII, startUDEC, Write_ASCII_1;
  wire [6:0] ASCII_t;
  wire [31:0] multiplexer_1_out, negator_1_out;

  // Probe on num
  or or_1 (or_1_out, demultiplexer_1_out0, END);
  Negator #(.width(32)) negator_1 (.in(num), .out(negator_1_out));
  D_Flip_Flop IDLE (.clk(CLK), .D(or_1_out), .Q(IDLE_q), .preset(RST));  // open: Qn, en, reset
  Demultiplexer #(.enable("false")) demultiplexer_1 (
    .out0(demultiplexer_1_out0), .out1(demultiplexer_1_out1), .in(IDLE_q), .sel(start));
  Multiplexer #(.width(32), .enable("false")) multiplexer_1 (
    .in0(num), .in1(negator_1_out), .out(multiplexer_1_out), .sel(num[31]));
  Demultiplexer #(.enable("false")) demultiplexer_2 (
    .out0(demultiplexer_2_out0), .out1(S_ASCII), .in(demultiplexer_1_out1), .sel(num[31]));
  or or_2 (or_2_out, demultiplexer_2_out0, S_ASCII);
  D_Flip_Flop IDLE_2 (.clk(CLK), .D(or_2_out), .Q(startUDEC), .reset(RST));  // open: Qn, preset, en
  PRINT_UDEC print_udec_1 (
    .num(multiplexer_1_out), .start(startUDEC), .CLK(CLK), .RST(RST), .ASCII(ASCII_t),
    .Write_ASCII(Write_ASCII_1), .\end (end_t));
  D_Flip_Flop IDLE_3 (.clk(CLK), .D(or_3_out), .Q(IDLE_3_q), .reset(RST));  // open: Qn, preset, en
  or or_3 (or_3_out, startUDEC, demultiplexer_3_out0);
  Demultiplexer #(.enable("false")) demultiplexer_3 (
    .out0(demultiplexer_3_out0), .out1(END), .in(IDLE_3_q), .sel(end_t));
  Multiplexer #(.width(7), .enable("false")) multiplexer_2 (
    .in0(ASCII_t), .in1(7'b0101101), .out(ASCII), .sel(S_ASCII));
  or or_4 (Write_ASCII, S_ASCII, Write_ASCII_1);

  // Other names for the same wires on the sheet: sign = num[31]; Write_ASCII_0 = S_ASCII
endmodule

module TEST_PRINT (
  input  [31:0] in_1,
  output out_2
);

  wire button_1_out, button_2_out, CLK, CLR, d_ff_1_q, Write_ASCII;
  wire [6:0] ASCII;

  Button button_1 (.out(button_1_out));
  Clock clock_1 (.out(CLK));
  D_Flip_Flop d_ff_1 (.clk(CLK), .D(1'b1), .Q(d_ff_1_q), .reset(button_1_out));  // open: Qn, preset, en
  D_Flip_Flop d_ff_2 (.clk(CLK), .D(d_ff_1_q), .Qn(CLR), .reset(button_1_out));  // open: Q, preset, en
  Button button_2 (.out(button_2_out));
  PRINT_UDEC print_udec_1 ();  // open: num, start, CLK, RST, ASCII, Write_ASCII, end
  PRINT_DEC print_dec_1 (
    .num(in_1), .start(button_2_out), .CLK(CLK), .RST(CLR), .ASCII(ASCII), .Write_ASCII(Write_ASCII),
    .END(out_2));
  TTY #(.rows(32), .cols(60)) tty_1 (.data(ASCII), .clk(CLK), .we(Write_ASCII), .clr(CLR));
endmodule

// Data \nPath
module Data_Path (
  input  [31:0] Data_In,
  input  L_A,
  input  L_B,
  input  L_PC,
  input  L_Dir_A_2,
  input  L_N,
  input  L_M,
  input  S_A,
  input  S_PC,
  input  [1:0] S_Dir_A_2,
  input  Clock,
  input  Clear,
  output [31:0] A1_i___A2_i,
  output [23:0] Dir_Memory,
  output PC____N___M___2,
  output jump
);

  wire comparator_1_eq;
  wire [23:0] Dir_A_2, Dir_A_2___1, divider_1_rem, multiplexer_2_out, multiplexer_3_out, N___M___2, PC,
       PC___1, PC___2;
  wire [31:0] A___B, B, M, multiplexer_1_out, N, N___M;

  // Probe on Data_In
  Multiplier #(.width(32)) multiplier_1 (.a(N), .b(M), .out(N___M));  // open: cin, cout
  Subtractor #(.width(32)) subtractor_1 (.a(A1_i___A2_i), .b(B), .out(A___B));  // open: bin, bout
  Adder #(.width(24)) adder_1 (.a(N___M[23:0]), .b(24'h2), .out(N___M___2));  // open: cin, cout
  Adder #(.width(24)) adder_2 (.a(PC), .b(24'h1), .out(PC___1));  // open: cin, cout
  Adder #(.width(24)) adder_3 (.a(Dir_A_2), .b(24'h1), .out(Dir_A_2___1));  // open: cin, cout
  Comparator #(.width(24), .mode("unsigned")) comparator_1 (
    .a(N___M___2), .b(PC), .eq(comparator_1_eq));  // open: gt, lt
  Subtractor #(.width(24)) subtractor_2 (.a(PC), .b(24'h2), .out(PC___2));  // open: bin, bout
  Divider #(.width(24)) divider_1 (.a(PC___2), .b(M[23:0]), .rem(divider_1_rem));  // open: out, upper
  // Probe on A___B
  not not_1 (PC____N___M___2, comparator_1_eq);
  Comparator #(.width(24), .mode("unsigned")) comparator_2 (
    .a(divider_1_rem), .b({24{1'b0}}), .eq(jump));  // open: gt, lt
  Multiplexer #(.width(32), .enable("false")) multiplexer_1 (
    .in0(Data_In), .in1(A___B), .out(multiplexer_1_out), .sel(S_A));
  Multiplexer #(.width(24), .enable("false")) multiplexer_2 (
    .in0(PC), .in1(PC___1), .out(multiplexer_2_out), .sel(S_PC));
  // Probe on A1_i___A2_i
  Register #(.width(32)) A (.D(multiplexer_1_out), .en(L_A), .Q(A1_i___A2_i), .clk(Clock), .clr(Clear));
  // Probe on PC
  Register #(.width(24)) u_PC (.D(multiplexer_2_out), .en(L_PC), .Q(PC), .clk(Clock), .clr(Clear));
  Register #(.width(32)) u_N (.D(Data_In), .en(L_N), .Q(N), .clk(Clock), .clr(Clear));
  // Probe on N
  Multiplexer #(.select(2), .width(24), .enable("false")) multiplexer_3 (
    .in0(Dir_A_2), .in1(N___M___2), .in2(Dir_A_2___1), .out(multiplexer_3_out), .sel(S_Dir_A_2));  // open: in3
  // Probe on B
  Register #(.width(32)) u_B (.D(Data_In), .en(L_B), .Q(B), .clk(Clock), .clr(Clear));
  // Probe on Dir_A_2
  Register #(.width(24)) u_Dir_A_2 (.D(multiplexer_3_out), .en(L_Dir_A_2), .Q(Dir_A_2), .clk(Clock), .clr(Clear));
  Register #(.width(32)) u_M (.D(Data_In), .en(L_M), .Q(M), .clk(Clock), .clr(Clear));
  // Probe on M
  // Probe on A1_i___A2_i
  Multiplexer #(.width(24), .enable("false")) multiplexer_4 (
    .in0(PC), .in1(Dir_A_2), .out(Dir_Memory), .sel(L_Dir_A_2));

  // Other names for the same wires on the sheet: A[31:0] = A1_i___A2_i; clk = Clock; clr = Clear; DI[31:0] = Data_In

  // Notes on the sheet:
  //   Inputs
  //   ALU
  //   Register File
  //   Outputs
endmodule

// Control \nUnit
module Control_Unit (
  input  PC____M___N___2,
  input  Done_print,
  input  Clock,
  input  Clear,
  input  Start,
  output L_A,
  output Write,
  output L_B,
  output Done,
  output L_PC,
  output L_Dir_A_2,
  output L_N,
  output L_M,
  output S_A,
  output S_PC,
  output [1:0] S_Dir_A_2
);

  wire d_ff_3_q, d_ff_7_q, demultiplexer_1_out0, demultiplexer_2_out0, demultiplexer_3_out0,
       demultiplexer_3_out1, demultiplexer_4_out1, END_q, IDLE_q, L_A0, or_1_out, or_5_out, or_7_out,
       or_8_out;

  or or_1 (or_1_out, demultiplexer_1_out0, demultiplexer_4_out1);
  D_Flip_Flop IDLE (.clk(Clock), .D(or_1_out), .Q(IDLE_q), .preset(Clear));  // open: Qn, en, reset
  Demultiplexer #(.enable("false")) demultiplexer_1 (.out0(demultiplexer_1_out0), .out1(L_N), .in(IDLE_q), .sel(Start));
  or or_2 (L_PC, L_N, L_M, S_A);
  D_Flip_Flop d_ff_1 (.clk(Clock), .D(L_N), .Q(L_M), .reset(Clear));  // open: Qn, preset, en
  or or_3 (S_PC, L_N, L_M, S_A);
  D_Flip_Flop d_ff_2 (.clk(Clock), .D(L_M), .Q(S_Dir_A_2[0]), .reset(Clear));  // open: Qn, preset, en
  or or_4 (L_Dir_A_2, S_Dir_A_2[0], L_B, S_A);
  or or_5 (or_5_out, S_Dir_A_2[0], demultiplexer_3_out1);
  Demultiplexer #(.enable("false")) demultiplexer_2 (
    .out0(demultiplexer_2_out0), .out1(L_A0), .in(d_ff_3_q), .sel(PC____M___N___2));
  D_Flip_Flop d_ff_3 (.clk(Clock), .D(or_5_out), .Q(d_ff_3_q), .reset(Clear));  // open: Qn, preset, en
  D_Flip_Flop d_ff_4 (.clk(Clock), .D(L_A0), .Q(L_B), .reset(Clear));  // open: Qn, preset, en
  or or_6 (L_A, L_A0, S_A);
  D_Flip_Flop d_ff_5 (.clk(Clock), .D(L_B), .Q(S_A), .reset(Clear));  // open: Qn, preset, en
  D_Flip_Flop d_ff_6 (.clk(Clock), .D(S_A), .Q(Write), .reset(Clear));  // open: Qn, preset, en
  D_Flip_Flop d_ff_7 (.clk(Clock), .D(or_7_out), .Q(d_ff_7_q), .reset(Clear));  // open: Qn, preset, en
  or or_7 (or_7_out, demultiplexer_3_out0, Write);
  Demultiplexer #(.enable("false")) demultiplexer_3 (
    .out0(demultiplexer_3_out0), .out1(demultiplexer_3_out1), .in(d_ff_7_q), .sel(Done_print));
  or or_8 (or_8_out, Done, demultiplexer_2_out0);
  D_Flip_Flop END (.clk(Clock), .D(or_8_out), .Q(END_q), .reset(Clear));  // open: Qn, preset, en
  Demultiplexer #(.enable("false")) demultiplexer_4 (.out0(Done), .out1(demultiplexer_4_out1), .in(END_q), .sel(Start));

  assign S_Dir_A_2[1] = S_A;

  // Other names for the same wires on the sheet: Clk = Clock; Clr = Clear; L_Dir_A_2_1 = L_B; bit_0 = S_Dir_A_2[0];
  //   L_Dir_A_2_0 = S_Dir_A_2[0]; bit_1 = S_A; L_A1 = S_A; L_Dir_A_2_2 = S_A; L_PC2 = S_A; S_PC2 = S_A; L_PC0 = L_N;
  //   S_PC0 = L_N; L_PC1 = L_M; S_PC1 = L_M

  // Notes on the sheet:
  //   Inputs
  //   Outputs
endmodule

// Restar \nMatrices
module Restar_Matrices (
  input  [31:0] Data_In,
  input  Done_print,
  input  Clock,
  input  Clear,
  input  Start,
  output [31:0] Data_Out,
  output [23:0] Dir_Input,
  output Done,
  output Write,
  output Jump
);

  wire control_unit_1_l_a, control_unit_1_l_b, control_unit_1_l_dir_a_2, control_unit_1_l_m,
       control_unit_1_l_n, control_unit_1_l_pc, control_unit_1_s_a, control_unit_1_s_pc, PC____N___M___2;
  wire [1:0] control_unit_1_s_dir_a_2;

  Control_Unit control_unit_1 (
    .L_A(control_unit_1_l_a), .Write(Write), .PC____M___N___2(PC____N___M___2), .L_B(control_unit_1_l_b),
    .Clock(Clock), .Done(Done), .L_PC(control_unit_1_l_pc), .Clear(Clear),
    .L_Dir_A_2(control_unit_1_l_dir_a_2), .Start(Start), .L_N(control_unit_1_l_n), .L_M(control_unit_1_l_m),
    .S_A(control_unit_1_s_a), .S_PC(control_unit_1_s_pc), .S_Dir_A_2(control_unit_1_s_dir_a_2),
    .Done_print(Done_print));
  Data_Path data_path_1 (
    .Data_In(Data_In), .L_A(control_unit_1_l_a), .L_B(control_unit_1_l_b), .L_PC(control_unit_1_l_pc),
    .L_Dir_A_2(control_unit_1_l_dir_a_2), .L_N(control_unit_1_l_n), .L_M(control_unit_1_l_m),
    .S_A(control_unit_1_s_a), .S_PC(control_unit_1_s_pc), .S_Dir_A_2(control_unit_1_s_dir_a_2),
    .Clock(Clock), .Clear(Clear), .A1_i___A2_i(Data_Out), .Dir_Memory(Dir_Input),
    .PC____N___M___2(PC____N___M___2), .jump(Jump));
  // Probe on Data_Out
  // Probe on Dir_Input

  // Other names for the same wires on the sheet: Clk = Clock; Clr = Clear; DI[31:0] = Data_In

  // Notes on the sheet:
  //   Inputs
  //   Outputs
endmodule
