// Logisim project BigASM.circ as structural Verilog
module BOARD_BIG_ASM (
  output out_1
);

  wire button_1_out, CLK, CLR, d_ff_1_q, not_1_out, Write, Write_ASCII;
  wire [6:0] ASCII;
  wire [7:0] counter_1_q;
  wire [23:0] Dir_INPUT, Dir_MEMORY;
  wire [31:0] INPUT, MEMORY_IN, MEMORY_OUT;

  Button button_1 (.out(button_1_out));
  Clock clock_1 (.out(CLK));
  D_Flip_Flop d_ff_1 (.clk(CLK), .D(1'b1), .Q(d_ff_1_q), .reset(button_1_out));  // open: Qn, preset, en
  D_Flip_Flop d_ff_2 (.clk(CLK), .D(d_ff_1_q), .Qn(CLR), .reset(button_1_out));  // open: Q, preset, en
  BIG_ASM big_asm_1 (
    .DATA_INPUT(INPUT), .MEMORY_IN(MEMORY_OUT), .CLK(CLK), .CLR(CLR), .DIR_INPUT(Dir_INPUT),
    .MEMORY_OUT(MEMORY_IN), .DIR_MEMORY(Dir_MEMORY), .Write_OUTPUT(Write), .ASCII(ASCII),
    .Write_ASCII(Write_ASCII), .END(out_1));
  MEMORY memory_1 (.DIR(Dir_MEMORY), .DATA_IN(MEMORY_IN), .WRITE(Write), .CLK(CLK), .CLR(CLR), .DATA_OUT(MEMORY_OUT));
  INPUT input_1 (.DIR(Dir_INPUT), .CLK(CLK), .DATA_OUT(INPUT));
  Counter counter_1 (.load(1'b0), .count(not_1_out), .Q(counter_1_q), .clk(CLK), .clr(CLR));  // open: D, carry
  not not_1 (not_1_out, out_1);
  // Probe on INPUT
  // Probe on counter_1_q
  TTY #(.rows(32), .cols(60)) tty_1 (.data(ASCII), .clk(CLK), .we(Write_ASCII), .clr(CLR));

  // Other names for the same wires on the sheet: END = out_1

  // Notes on the sheet:
  //   COUNTER
  //   BOARD
endmodule

module INPUT (
  input  [23:0] DIR,
  input  CLK,
  output [31:0] DATA_OUT
);

  RAM #(.addrWidth(24), .dataWidth(32)) ram_1 (.addr(DIR), .data(DATA_OUT), .clk(CLK), .ld(1'b1));  // open: sel, clr
endmodule

module MEMORY (
  input  [23:0] DIR,
  input  [31:0] DATA_IN,
  input  WRITE,
  input  CLK,
  input  CLR,
  output [31:0] DATA_OUT
);

  RAM #(.addrWidth(24), .dataWidth(32), .bus("separate")) ram_1 (
    .addr(DIR), .din(DATA_IN), .data(DATA_OUT), .str(WRITE), .clk(CLK), .clr(CLR));  // open: sel, ld
endmodule

module BIG_ASM (
  input  [31:0] DATA_INPUT,
  input  [31:0] MEMORY_IN,
  input  CLK,
  input  CLR,
  output [23:0] DIR_INPUT,
  output [31:0] MEMORY_OUT,
  output [23:0] DIR_MEMORY,
  output Write_OUTPUT,
  output [6:0] ASCII,
  output Write_ASCII,
  output END
);

  wire and_1_out, d_ff_1_q, d_ff_3_q, demultiplexer_1_out0, demultiplexer_2_out0, demultiplexer_2_out1,
       demultiplexer_4_out0, demultiplexer_5_out1, end_print, END_q, end_t, false, i___n, IDLE_q, L_i, L_N,
       L_n_t, or_1_out, or_2_out, or_3_out, or_4_out, or_5_out, or_7_out, or_8_out, PRINT_q, start, WHILE_q,
       write;
  wire [6:0] ASCII_t;
  wire [23:0] build_heap_1_dir_memory;
  wire [31:0] i, i___1, N, number;

  D_Flip_Flop d_ff_1 (.clk(CLK), .D(1'b1), .Q(d_ff_1_q), .reset(CLR));  // open: Qn, preset, en
  or or_1 (or_1_out, demultiplexer_1_out0, demultiplexer_5_out1);
  D_Flip_Flop d_ff_2 (.clk(CLK), .D(d_ff_1_q), .Qn(start), .reset(CLR));  // open: Q, preset, en
  D_Flip_Flop IDLE (.clk(CLK), .D(or_1_out), .Q(IDLE_q), .preset(CLR));  // open: Qn, en, reset
  Demultiplexer #(.enable("false")) demultiplexer_1 (
    .out0(demultiplexer_1_out0), .out1(L_n_t), .in(IDLE_q), .sel(start));
  // Probe on MEMORY_IN
  or or_2 (or_2_out, false, end_t);
  // Probe on number
  and and_1 (and_1_out, END, ~or_2_out);  // AND_Gate
  D_Flip_Flop d_ff_3 (.clk(CLK), .D(or_3_out), .Q(d_ff_3_q), .reset(CLR));  // open: Qn, preset, en
  or or_3 (or_3_out, demultiplexer_2_out0, L_n_t);
  Demultiplexer #(.enable("false")) demultiplexer_2 (
    .out0(demultiplexer_2_out0), .out1(demultiplexer_2_out1), .in(d_ff_3_q), .sel(END));
  Build_Heap build_heap_1 (
    .DATA_INPUT(DATA_INPUT), .MEMORY_IN(MEMORY_IN), .Clock(CLK), .Clear(CLR), .Start(start),
    .DIR_INPUT(DIR_INPUT), .MEMORY_OUT(MEMORY_OUT), .DIR_MEMORY(build_heap_1_dir_memory),
    .Write_OUTPUT(Write_OUTPUT), .END(END));
  or or_4 (or_4_out, CLR, L_N);
  or or_5 (or_5_out, demultiplexer_2_out1, L_i);
  PRINT_DEC print_dec_1 (
    .num(number), .start(and_1_out), .CLK(CLK), .RST(or_4_out), .ASCII(ASCII_t), .Write_ASCII(write),
    .END(end_print));
  D_Flip_Flop WHILE (.clk(CLK), .D(or_5_out), .Q(WHILE_q), .reset(CLR));  // open: Qn, preset, en
  Demultiplexer #(.enable("false")) demultiplexer_3 (.out0(false), .out1(L_N), .in(WHILE_q), .sel(i___n));
  Multiplexer #(.width(24), .enable("false")) multiplexer_1 (
    .in0(build_heap_1_dir_memory), .in1(i[23:0]), .out(DIR_MEMORY), .sel(END));
  Multiplexer #(.width(7), .enable("false")) multiplexer_2 (
    .in0(ASCII_t), .in1(7'b0100000), .out(ASCII), .sel(end_print));
  or or_6 (Write_ASCII, write, end_print);
  or or_7 (or_7_out, demultiplexer_4_out0, L_N);
  D_Flip_Flop PRINT (.clk(CLK), .D(or_7_out), .Q(PRINT_q), .reset(CLR));  // open: Qn, preset, en
  Demultiplexer #(.enable("false")) demultiplexer_4 (
    .out0(demultiplexer_4_out0), .out1(L_i), .in(PRINT_q), .sel(end_print));
  // Probe on DIR_MEMORY
  // Probe on number
  Register #(.width(32)) u_Number (.D(MEMORY_IN), .en(L_N), .Q(number), .clk(CLK), .clr(CLR));
  D_Flip_Flop u_END (.clk(CLK), .D(or_8_out), .Q(END_q), .reset(CLR));  // open: Qn, preset, en
  or or_8 (or_8_out, end_t, false);
  Demultiplexer #(.enable("false")) demultiplexer_5 (
    .out0(end_t), .out1(demultiplexer_5_out1), .in(END_q), .sel(start));
  // Probe on i
  Register #(.width(32)) Iterador (.D(i___1), .en(L_i), .Q(i), .clk(CLK), .clr(CLR));
  Adder #(.width(32)) adder_1 (.a(i), .b(32'h1), .out(i___1));  // open: cin, cout
  // Probe on N
  Register #(.width(32)) Length (.D(DATA_INPUT), .en(L_n_t), .Q(N), .clk(CLK), .clr(CLR));
  Comparator #(.width(32), .mode("unsigned")) comparator_1 (.a(i), .b(N), .lt(i___n));  // open: gt, eq

  // Other names for the same wires on the sheet: done = END; Memory[31:0] = MEMORY_IN; n_t[31:0] = DATA_INPUT;
  //   reset = L_N
endmodule

module PRINT_UDEC (
  input  [31:0] num,
  input  start,
  input  CLK,
  input  RST,
  output [6:0] ASCII,
  output Write_ASCII,
  output \end 
);

  wire _0_c, _0_n, demultiplexer_1_out0, demultiplexer_2_out0, demultiplexer_2_out1, demultiplexer_3_out0,
       demultiplexer_3_out1, IDLE_2_q, IDLE_3_q, IDLE_4_q, IDLE_q, Lc, Lc_0, Ln, Ln_0, or_1_out;
  wire [23:0] bit_extender_1_out;
  wire [31:0] c, c___1, c___1_t, divider_1_rem, memory_1_data_out, multiplexer_1_out, multiplexer_2_out,
       multiplexer_3_out, n, n___10, n___10___48;

  Multiplexer #(.width(32), .enable("false")) multiplexer_1 (
    .in0(num), .in1(n___10), .out(multiplexer_1_out), .sel(Lc_0));
  Divider #(.width(32)) divider_1 (.a(n), .b(32'ha), .out(n___10), .rem(divider_1_rem));  // open: upper
  Adder #(.width(32)) adder_1 (.a(divider_1_rem), .b(32'h30), .out(n___10___48));  // open: cin, cout
  or or_1 (or_1_out, demultiplexer_1_out0, \end );
  Register #(.width(32)) u_n (.D(multiplexer_1_out), .en(Ln), .Q(n), .clk(CLK), .clr(RST));
  D_Flip_Flop IDLE (.clk(CLK), .D(or_1_out), .Q(IDLE_q), .preset(RST));  // open: Qn, en, reset
  Demultiplexer #(.enable("false")) demultiplexer_1 (
    .out0(demultiplexer_1_out0), .out1(Ln_0), .in(IDLE_q), .sel(start));
  or or_2 (Write_ASCII, demultiplexer_3_out0, demultiplexer_2_out1);
  Multiplexer #(.width(32), .enable("false")) multiplexer_2 (
    .in0(c___1), .in1(c___1_t), .out(multiplexer_2_out), .sel(Write_ASCII));
  Adder #(.width(32)) adder_2 (.a(c), .b(32'h1), .out(c___1));  // open: cin, cout
  Subtractor #(.width(32)) subtractor_1 (.a(c), .b(32'h1), .out(c___1_t));  // open: bin, bout
  D_Flip_Flop IDLE_2 (.clk(CLK), .D(Ln_0), .Q(IDLE_2_q), .reset(RST));  // open: Qn, preset, en
  Register #(.width(32)) u_c (.D(multiplexer_2_out), .en(Lc), .Q(c), .clk(CLK), .clr(RST));
  or or_3 (Lc_0, IDLE_2_q, demultiplexer_3_out1);
  Multiplexer #(.width(32), .enable("false")) multiplexer_3 (
    .in0(c), .in1(c___1_t), .out(multiplexer_3_out), .sel(Write_ASCII));
  Comparator #(.width(32), .mode("unsigned")) comparator_1 (.a({32{1'b0}}), .b(n), .lt(_0_n));  // open: gt, eq
  Comparator #(.width(32), .mode("unsigned")) comparator_2 (.a({32{1'b0}}), .b(c), .lt(_0_c));  // open: gt, eq
  D_Flip_Flop IDLE_3 (.clk(CLK), .D(Write_ASCII), .Q(IDLE_3_q), .reset(RST));  // open: Qn, preset, en
  Demultiplexer #(.enable("false")) demultiplexer_2 (
    .out0(demultiplexer_2_out0), .out1(demultiplexer_2_out1), .in(IDLE_3_q), .sel(_0_c));
  Bit_Extender #(.in_width(32), .out_width(24)) bit_extender_1 (.in(multiplexer_3_out), .out(bit_extender_1_out));
  D_Flip_Flop IDLE_4 (.clk(CLK), .D(Lc_0), .Q(IDLE_4_q), .reset(RST));  // open: Qn, preset, en
  or or_4 (Lc, Lc_0, Write_ASCII);
  or or_5 (Ln, Ln_0, Lc_0);
  Demultiplexer #(.enable("false")) demultiplexer_3 (
    .out0(demultiplexer_3_out0), .out1(demultiplexer_3_out1), .in(IDLE_4_q), .sel(_0_n));
  D_Flip_Flop IDLE_5 (.clk(CLK), .D(demultiplexer_2_out0), .Q(\end ), .reset(RST));  // open: Qn, preset, en
  MEMORY memory_1 (
    .DIR(bit_extender_1_out), .DATA_IN(n___10___48), .WRITE(Lc_0), .CLK(CLK), .CLR(RST),
    .DATA_OUT(memory_1_data_out));
  Bit_Extender #(.in_width(32), .out_width(7)) bit_extender_2 (.in(memory_1_data_out), .out(ASCII));

  // Other names for the same wires on the sheet: Lc_1 = Write_ASCII; Sc = Write_ASCII; Ln_1 = Lc_0; Sn = Lc_0;
  //   Write = Lc_0
endmodule

module PRINT_DEC (
  input  [31:0] num,
  input  start,
  input  CLK,
  input  RST,
  output [6:0] ASCII,
  output Write_ASCII,
  output END
);

  wire demultiplexer_1_out0, demultiplexer_1_out1, demultiplexer_2_out0, demultiplexer_3_out0, end_t,
       IDLE_3_q, IDLE_q, or_1_out, or_2_out, or_3_out, S_ASCII, startUDEC, Write_ASCII_1;
  wire [6:0] ASCII_t;
  wire [31:0] multiplexer_1_out, negator_1_out;

  or or_1 (or_1_out, demultiplexer_1_out0, END);
  Negator #(.width(32)) negator_1 (.in(num), .out(negator_1_out));
  D_Flip_Flop IDLE (.clk(CLK), .D(or_1_out), .Q(IDLE_q), .preset(RST));  // open: Qn, en, reset
  Demultiplexer #(.enable("false")) demultiplexer_1 (
    .out0(demultiplexer_1_out0), .out1(demultiplexer_1_out1), .in(IDLE_q), .sel(start));
  Multiplexer #(.width(32), .enable("false")) multiplexer_1 (
    .in0(num), .in1(negator_1_out), .out(multiplexer_1_out), .sel(num[31]));
  Demultiplexer #(.enable("false")) demultiplexer_2 (
    .out0(demultiplexer_2_out0), .out1(S_ASCII), .in(demultiplexer_1_out1), .sel(num[31]));
  or or_2 (or_2_out, demultiplexer_2_out0, S_ASCII);
  D_Flip_Flop IDLE_2 (.clk(CLK), .D(or_2_out), .Q(startUDEC), .reset(RST));  // open: Qn, preset, en
  PRINT_UDEC print_udec_1 (
    .num(multiplexer_1_out), .start(startUDEC), .CLK(CLK), .RST(RST), .ASCII(ASCII_t),
    .Write_ASCII(Write_ASCII_1), .\end (end_t));
  D_Flip_Flop IDLE_3 (.clk(CLK), .D(or_3_out), .Q(IDLE_3_q), .reset(RST));  // open: Qn, preset, en
  or or_3 (or_3_out, startUDEC, demultiplexer_3_out0);
  Demultiplexer #(.enable("false")) demultiplexer_3 (
    .out0(demultiplexer_3_out0), .out1(END), .in(IDLE_3_q), .sel(end_t));
  Multiplexer #(.width(7), .enable("false")) multiplexer_2 (
    .in0(ASCII_t), .in1(7'b0101101), .out(ASCII), .sel(S_ASCII));
  or or_4 (Write_ASCII, S_ASCII, Write_ASCII_1);

  // Other names for the same wires on the sheet: sign = num[31]; Write_ASCII_0 = S_ASCII
endmodule

module TEST_PRINT (
  input  [31:0] in_1,
  output out_2
);

  wire button_1_out, button_2_out, CLK, CLR, d_ff_1_q, Write_ASCII;
  wire [6:0] ASCII;

  Button button_1 (.out(button_1_out));
  Clock clock_1 (.out(CLK));
  D_Flip_Flop d_ff_1 (.clk(CLK), .D(1'b1), .Q(d_ff_1_q), .reset(button_1_out));  // open: Qn, preset, en
  D_Flip_Flop d_ff_2 (.clk(CLK), .D(d_ff_1_q), .Qn(CLR), .reset(button_1_out));  // open: Q, preset, en
  Button button_2 (.out(button_2_out));
  PRINT_UDEC print_udec_1 ();  // open: num, start, CLK, RST, ASCII, Write_ASCII, end
  PRINT_DEC print_dec_1 (
    .num(in_1), .start(button_2_out), .CLK(CLK), .RST(CLR), .ASCII(ASCII), .Write_ASCII(Write_ASCII),
    .END(out_2));
  TTY #(.rows(32), .cols(60)) tty_1 (.data(ASCII), .clk(CLK), .we(Write_ASCII), .clr(CLR));
endmodule

// Data \nPath
module Data_Path (
  input  [31:0] Data_In,
  input  [31:0] Memory_In,
  input  L_N,
  input  L_M,
  input  S_M,
  input  L_T,
  input  L_actual,
  input  L_I,
  input  [1:0] S_I,
  input  L_index,
  input  [1:0] S_index,
  input  Clock,
  input  Copy,
  input  L_i_2,
  input  S_i_2,
  input  Clear,
  input  [1:0] S_Dir,
  input  L_PC,
  input  S_PC,
  input  S_T,
  input  Swap,
  output I____N,
  output [31:0] Memory_Out,
  output i____0,
  output index___1___N,
  output [23:0] Dir_Memory,
  output M____T,
  output [23:0] Dir_Input,
  output actual___M,
  output index____N___2
);

  wire comparator_1_eq, comparator_1_lt, comparator_2_eq, comparator_2_gt, comparator_6_eq, comparator_6_gt,
       M___T;
  wire [23:0] multiplexer_5_out, PC___1, PC___1_t;
  wire [31:0] _2___i, _2___i___1, _2___index, _2___index___1, actual, bit_extender_1_out, I, I___1, i___1_t,
       i_t, index, index___1, index_t, M, Memory, min_M__T, multiplexer_1_out, multiplexer_2_out,
       multiplexer_3_out, multiplexer_4_out, multiplexer_6_out, multiplexer_7_out, N, N___2, N___2___1, T;
  wire [31:24] multiplexer_9_out;

  // Probe on M
  Multiplexer #(.width(32), .enable("false")) multiplexer_1 (
    .in0(Memory), .in1(min_M__T), .out(multiplexer_1_out), .sel(S_M));
  // Probe on Data_In
  Register #(.width(32)) u_N (.D(Data_In), .en(L_N), .Q(N), .clk(Clock), .clr(Clear));
  Register #(.width(32)) u_M (.D(multiplexer_1_out), .en(L_M), .Q(M), .clk(Clock), .clr(Clear));
  Register #(.width(32)) u_T (.D(Memory), .en(L_T), .Q(T), .clk(Clock), .clr(Clear));
  Register #(.width(32)) u_actual (.D(Memory), .en(L_actual), .Q(actual), .clk(Clock), .clr(Clear));
  // Probe on Memory_In
  // Probe on T
  // Probe on actual
  Multiplexer #(.select(2), .width(32), .enable("false")) multiplexer_2 (
    .in0(32'h1), .in1(i_t), .in2(I___1), .in3(index), .out(multiplexer_2_out), .sel(S_I));
  Multiplexer #(.select(2), .width(32), .enable("false")) multiplexer_3 (
    .in0(_2___i___1), .in1(index___1), .in2(_2___index___1), .out(multiplexer_3_out), .sel(S_index));  // open: in3
  Multiplexer #(.width(32), .enable("false")) multiplexer_4 (
    .in0(N___2___1), .in1(i___1_t), .out(multiplexer_4_out), .sel(S_i_2));
  Multiplexer #(.width(24), .enable("false")) multiplexer_5 (
    .in0(Dir_Input), .in1(PC___1), .out(multiplexer_5_out), .sel(S_PC));
  Register #(.width(32)) u_I (.D(multiplexer_2_out), .en(L_I), .Q(I), .clk(Clock), .clr(Clear));
  Register #(.width(32)) u_index (.D(multiplexer_3_out), .en(L_index), .Q(index), .clk(Clock), .clr(Clear));
  Register #(.width(32)) i_2 (.D(multiplexer_4_out), .en(L_i_2), .Q(i_t), .clk(Clock), .clr(Clear));
  Register #(.width(24)) PC (.D(multiplexer_5_out), .en(L_PC), .Q(Dir_Input), .clk(Clock), .clr(Clear));
  Multiplexer #(.width(32), .enable("false")) multiplexer_6 (.in0(actual), .in1(T), .out(multiplexer_6_out), .sel(S_T));
  assign bit_extender_1_out = {{8{1'b0}}, PC___1_t};  // Bit_Extender bit_extender_1
  // Probe on index
  // Probe on i_t
  Multiplexer #(.width(32), .enable("false")) multiplexer_7 (
    .in0(Memory_In), .in1(multiplexer_6_out), .out(multiplexer_7_out), .sel(Swap));
  Multiplexer #(.width(32), .enable("false")) multiplexer_8 (
    .in0(multiplexer_7_out), .in1(Data_In), .out(Memory_Out), .sel(Copy));
  Multiplexer #(.select(2), .width(32), .enable("false")) multiplexer_9 (
    .in0(bit_extender_1_out), .in1(index), .in2(I), .in3(index___1), .out({multiplexer_9_out, Dir_Memory}),
    .sel(S_Dir));
  // Probe on {multiplexer_9_out, Dir_Memory}
  Comparator #(.width(32)) comparator_1 (.a(I), .b(N), .eq(comparator_1_eq), .lt(comparator_1_lt));  // open: gt
  Comparator #(.width(32)) comparator_2 (
    .a(i_t), .b({32{1'b0}}), .gt(comparator_2_gt), .eq(comparator_2_eq));  // open: lt
  Comparator #(.width(32)) comparator_3 (.a(index___1), .b(N), .lt(index___1___N));  // open: gt, eq
  Comparator #(.width(32)) comparator_4 (.a(M), .b(T), .gt(M___T), .eq(M____T));  // open: lt
  Multiplexer #(.width(32), .enable("false")) multiplexer_10 (.in0(M), .in1(T), .out(min_M__T), .sel(M___T));
  Adder #(.width(24)) adder_1 (.a(Dir_Input), .b(24'h1), .out(PC___1));  // open: cin, cout
  // Probe on Memory_Out
  or or_1 (I____N, comparator_1_eq, comparator_1_lt);
  or or_2 (i____0, comparator_2_gt, comparator_2_eq);
  Comparator #(.width(32)) comparator_5 (.a(actual), .b(M), .gt(actual___M));  // open: eq, lt
  or or_3 (index____N___2, comparator_6_gt, comparator_6_eq);
  Comparator #(.width(32)) comparator_6 (
    .a(index_t), .b(N___2), .gt(comparator_6_gt), .eq(comparator_6_eq));  // open: lt
  Adder #(.width(32)) adder_2 (.a(index), .b(32'h1), .out(index___1));  // open: cin, cout
  Divider #(.width(32)) divider_1 (.a(N), .b(32'h2), .out(N___2));  // open: upper, rem
  Adder #(.width(32)) adder_3 (.a(I), .b(32'h1), .out(I___1));  // open: cin, cout
  Subtractor #(.width(32)) subtractor_1 (.a(i_t), .b(32'h1), .out(i___1_t));  // open: bin, bout
  Multiplier #(.width(32)) multiplier_1 (.a(i_t), .b(32'h2), .out(_2___i));  // open: cin, cout
  Multiplier #(.width(32)) multiplier_2 (.a(index), .b(32'h2), .out(_2___index));  // open: cin, cout
  Adder #(.width(32)) adder_4 (.a(_2___i), .b(32'h1), .out(_2___i___1));  // open: cin, cout
  Adder #(.width(32)) adder_5 (.a(_2___index), .b(32'h1), .out(_2___index___1));  // open: cin, cout
  Subtractor #(.width(24)) subtractor_2 (.a(Dir_Input), .b(24'h1), .out(PC___1_t));  // open: bin, bout
  Subtractor #(.width(32)) subtractor_3 (.a(N___2), .b(32'h1), .out(N___2___1));  // open: bin, bout
  // Probe on _2___index___1

  // Other names for the same wires on the sheet: clk = Clock; clr = Clear; DI[31:0] = Data_In; L_i_t = L_i_2;
  //   Memory_t[31:0] = Memory_In; PC[23:0] = Dir_Input; S_i_t = S_i_2

  // Notes on the sheet:
  //   Inputs
  //   Register File
  //   ALU
  //   Outputs
endmodule

// Control \nUnit
module Control_Unit (
  input  Clock,
  input  Clear,
  input  Start,
  input  I____N,
  input  i____0,
  input  index___1___N,
  input  M____T,
  input  actual___M,
  input  index____N___2,
  output L_N,
  output L_M,
  output S_M,
  output L_T,
  output L_actual,
  output L_I,
  output [1:0] S_I,
  output L_index,
  output [1:0] S_index,
  output L_i_2,
  output S_i_2,
  output L_PC,
  output S_PC,
  output Copy,
  output [1:0] S_Dir,
  output Swap,
  output Write,
  output done,
  output S_T
);

  wire \continue , d_ff_1_q, d_ff_6_q, d_ff_7_q, d_ff_8_q, d_ff_11_q, demultiplexer_1_out1,
       demultiplexer_2_out0, demultiplexer_3_out0, demultiplexer_5_out0, demultiplexer_6_out0,
       demultiplexer_7_out0, demultiplexer_8_out0, demultiplexer_9_out0, demultiplexer_10_out1, Dir_1, Dir_3,
       END_q, Heapyfy, IDLE_q, L_actual0, L_actual1, L_i0_t, L_index_1, L_index_3, L_M0, L_M1, L_M2, L_M3,
       L_T0, L_T1, L_T_3, or_1_out, or_9_out, or_16_out, or_17_out, or_22_out, or_24_out, S_Dir_1_1,
       WHILE_2_q, WHILE_3_q, WHILE_q;

  or or_1 (or_1_out, demultiplexer_2_out0, demultiplexer_10_out1);
  D_Flip_Flop d_ff_1 (.clk(Clock), .D(S_Dir_1_1), .Q(d_ff_1_q), .reset(Clear));  // open: Qn, preset, en
  Demultiplexer #(.enable("false")) demultiplexer_1 (
    .out0(S_index[1]), .out1(demultiplexer_1_out1), .in(d_ff_1_q), .sel(index____N___2));
  D_Flip_Flop IDLE (.clk(Clock), .D(or_1_out), .Q(IDLE_q), .preset(Clear));  // open: Qn, en, reset
  Demultiplexer #(.enable("false")) demultiplexer_2 (.out0(demultiplexer_2_out0), .out1(L_N), .in(IDLE_q), .sel(Start));
  D_Flip_Flop d_ff_2 (.clk(Clock), .D(Heapyfy), .Q(L_M0), .reset(Clear));  // open: Qn, preset, en
  D_Flip_Flop d_ff_3 (.clk(Clock), .D(L_T0), .Q(L_M1), .reset(Clear));  // open: Qn, preset, en
  D_Flip_Flop d_ff_4 (.clk(Clock), .D(S_index[1]), .Q(L_M2), .reset(Clear));  // open: Qn, preset, en
  or or_2 (L_I, L_N, Copy, Heapyfy, S_index[1]);
  or or_3 (L_i_2, L_i0_t, S_i_2);
  or or_4 (L_PC, L_N, Copy);
  or or_5 (L_actual, L_actual0, L_actual1);
  or or_6 (L_T, L_T0, L_T_3, L_T1);
  or or_7 (S_PC, L_N, Copy);
  or or_8 (S_index[0], L_index_1, L_index_3);
  D_Flip_Flop d_ff_5 (.clk(Clock), .D(L_M0), .Q(L_actual0), .reset(Clear));  // open: Qn, preset, en
  or or_9 (or_9_out, L_N, Copy);
  D_Flip_Flop d_ff_6 (.clk(Clock), .D(L_M1), .Q(d_ff_6_q), .reset(Clear));  // open: Qn, preset, en
  Demultiplexer #(.enable("false")) demultiplexer_3 (
    .out0(demultiplexer_3_out0), .out1(L_index_1), .in(d_ff_6_q), .sel(M____T));
  D_Flip_Flop d_ff_7 (.clk(Clock), .D(L_M2), .Q(d_ff_7_q), .reset(Clear));  // open: Qn, preset, en
  or or_10 (S_I[0], Heapyfy, S_index[1]);
  or or_11 (S_I[1], Copy, S_index[1]);
  D_Flip_Flop WHILE (.clk(Clock), .D(or_9_out), .Q(WHILE_q), .reset(Clear));  // open: Qn, preset, en
  Demultiplexer #(.enable("false")) demultiplexer_4 (.out0(L_i0_t), .out1(Copy), .in(WHILE_q), .sel(I____N));
  D_Flip_Flop d_ff_8 (.clk(Clock), .D(L_actual0), .Q(d_ff_8_q), .reset(Clear));  // open: Qn, preset, en
  Demultiplexer #(.enable("false")) demultiplexer_5 (
    .out0(demultiplexer_5_out0), .out1(L_T1), .in(d_ff_7_q), .sel(index___1___N));
  or or_12 (L_index, Heapyfy, L_index_1, S_index[1], L_index_3);
  or or_13 (L_M, L_M0, L_M1, L_M2, L_M3);
  or or_14 (Write, S_T, Copy, S_Dir_1_1);
  or or_15 (S_M, L_M1, L_M3);
  Demultiplexer #(.enable("false")) demultiplexer_6 (
    .out0(demultiplexer_6_out0), .out1(L_T0), .in(d_ff_8_q), .sel(index___1___N));
  or or_16 (or_16_out, S_i_2, L_i0_t);
  D_Flip_Flop d_ff_9 (.clk(Clock), .D(L_T1), .Q(L_M3), .reset(Clear));  // open: Qn, preset, en
  D_Flip_Flop WHILE_2 (.clk(Clock), .D(or_16_out), .Q(WHILE_2_q), .reset(Clear));  // open: Qn, preset, en
  Demultiplexer #(.enable("false")) demultiplexer_7 (
    .out0(demultiplexer_7_out0), .out1(Heapyfy), .in(WHILE_2_q), .sel(i____0));
  or or_17 (or_17_out, demultiplexer_6_out0, demultiplexer_3_out0, L_index_1, \continue );
  or or_18 (Swap, S_Dir_1_1, S_T);
  D_Flip_Flop d_ff_10 (.clk(Clock), .D(L_T_3), .Q(S_T), .reset(Clear));  // open: Qn, preset, en
  D_Flip_Flop d_ff_11 (.clk(Clock), .D(L_M3), .Q(d_ff_11_q), .reset(Clear));  // open: Qn, preset, en
  Demultiplexer #(.enable("false")) demultiplexer_8 (
    .out0(demultiplexer_8_out0), .out1(L_index_3), .in(d_ff_11_q), .sel(M____T));
  or or_19 (Dir_1, L_M0, S_Dir_1_1, L_M2, L_T_3);
  or or_20 (Dir_3, L_T1, L_T0);
  or or_21 (S_Dir[0], Dir_1, Dir_3);
  or or_22 (or_22_out, L_actual0, L_actual1, S_T);
  or or_23 (S_Dir[1], or_22_out, Dir_3);
  or or_24 (or_24_out, done, demultiplexer_7_out0);
  D_Flip_Flop WHILE_3 (.clk(Clock), .D(or_17_out), .Q(WHILE_3_q), .reset(Clear));  // open: Qn, preset, en
  Demultiplexer #(.enable("false")) demultiplexer_9 (
    .out0(demultiplexer_9_out0), .out1(L_T_3), .in(WHILE_3_q), .sel(actual___M));
  D_Flip_Flop END (.clk(Clock), .D(or_24_out), .Q(END_q), .reset(Clear));  // open: Qn, preset, en
  Demultiplexer #(.enable("false")) demultiplexer_10 (
    .out0(done), .out1(demultiplexer_10_out1), .in(END_q), .sel(Start));
  D_Flip_Flop d_ff_12 (.clk(Clock), .D(S_T), .Q(S_Dir_1_1), .reset(Clear));  // open: Qn, preset, en
  or or_25 (L_actual1, demultiplexer_8_out0, L_index_3);
  or or_26 (\continue , demultiplexer_5_out0, L_actual1);
  or or_27 (S_i_2, demultiplexer_9_out0, demultiplexer_1_out1);

  // Other names for the same wires on the sheet: clk = Clock; clr = Clear; end_Heapyfy = S_i_2; L_i1_t = S_i_2;
  //   S_i_t = S_i_2; L_i_t = L_i_2; S_Dir_1 = L_M0; S_Dir_1_0 = L_T_3; S_Dir_1_2 = L_M2; S_Dir_2 = L_actual0;
  //   S_Dir_2_1 = L_actual1; S_Dir_3 = L_T0; S_Dir_3_0 = L_T1; L_I2 = Heapyfy; L_index_0 = Heapyfy; S_I_1 = Heapyfy;
  //   L_I3 = S_index[1]; L_index_2 = S_index[1]; S_I3 = S_index[1]; S_index_2 = S_index[1]; S_index_1 = L_index_1;
  //   S_index_1_0 = L_index_3; S_M0 = L_M1; S_M1 = L_M3; L_I0 = L_N; L_PC0 = L_N; S_PC0 = L_N; S_Dir_2_0 = S_T;
  //   Swap_0 = S_T; Write_0 = S_T; Swap_1 = S_Dir_1_1; Write_1 = S_Dir_1_1; L_I1 = Copy; L_PC1 = Copy; S_I_2_t = Copy;
  //   S_PC1 = Copy; write_t = Copy

  // Notes on the sheet:
  //   Inputs
  //   Outputs
endmodule

// Build \nHeap
module Build_Heap (
  input  [31:0] DATA_INPUT,
  input  [31:0] MEMORY_IN,
  input  Clock,
  input  Clear,
  input  Start,
  output [23:0] DIR_INPUT,
  output [31:0] MEMORY_OUT,
  output [23:0] DIR_MEMORY,
  output Write_OUTPUT,
  output END
);

  wire actual___M, control_unit_1_l_actual, control_unit_1_l_i, control_unit_1_l_i_2, control_unit_1_l_index,
       control_unit_1_l_m, control_unit_1_l_n, control_unit_1_l_pc, control_unit_1_l_t, control_unit_1_s_i_2,
       control_unit_1_s_m, control_unit_1_s_pc, control_unit_1_s_t, copy, i____0, I____N, index___1___N,
       index____N___2, M____T, swap;
  wire [1:0] control_unit_1_s_dir, control_unit_1_s_i, control_unit_1_s_index;

  Control_Unit control_unit_1 (
    .Clock(Clock), .Clear(Clear), .Start(Start), .I____N(I____N), .i____0(i____0),
    .index___1___N(index___1___N), .M____T(M____T), .actual___M(actual___M), .index____N___2(index____N___2),
    .L_N(control_unit_1_l_n), .L_M(control_unit_1_l_m), .S_M(control_unit_1_s_m), .L_T(control_unit_1_l_t),
    .L_actual(control_unit_1_l_actual), .L_I(control_unit_1_l_i), .S_I(control_unit_1_s_i),
    .L_index(control_unit_1_l_index), .S_index(control_unit_1_s_index), .L_i_2(control_unit_1_l_i_2),
    .S_i_2(control_unit_1_s_i_2), .L_PC(control_unit_1_l_pc), .S_PC(control_unit_1_s_pc), .Copy(copy),
    .S_Dir(control_unit_1_s_dir), .Swap(swap), .Write(Write_OUTPUT), .done(END), .S_T(control_unit_1_s_t));
  Data_Path data_path_1 (
    .Data_In(DATA_INPUT), .Memory_In(MEMORY_IN), .L_N(control_unit_1_l_n), .L_M(control_unit_1_l_m),
    .S_M(control_unit_1_s_m), .L_T(control_unit_1_l_t), .L_actual(control_unit_1_l_actual),
    .L_I(control_unit_1_l_i), .S_I(control_unit_1_s_i), .L_index(control_unit_1_l_index),
    .S_index(control_unit_1_s_index), .Clock(Clock), .Copy(copy), .L_i_2(control_unit_1_l_i_2),
    .S_i_2(control_unit_1_s_i_2), .Clear(Clear), .S_Dir(control_unit_1_s_dir), .L_PC(control_unit_1_l_pc),
    .S_PC(control_unit_1_s_pc), .Swap(swap), .I____N(I____N), .i____0(i____0), .index___1___N(index___1___N),
    .M____T(M____T), .actual___M(actual___M), .index____N___2(index____N___2), .Memory_Out(MEMORY_OUT),
    .Dir_Memory(DIR_MEMORY), .Dir_Input(DIR_INPUT), .S_T(control_unit_1_s_t));

  // Other names for the same wires on the sheet: clk = Clock; clr = Clear; DI[31:0] = DATA_INPUT;
  //   Memory[31:0] = MEMORY_IN; write = Write_OUTPUT

  // Notes on the sheet:
  //   Inputs
  //   Outputs
endmodule
