// Logisim project BigASM.circ as structural Verilog
module BOARD_BIG_ASM (
  output out_1
);

  wire button_1_out, CLK, CLR, d_ff_1_q, not_1_out, Write, Write_ASCII;
  wire [6:0] ASCII;
  wire [7:0] counter_1_q;
  wire [23:0] Dir_INPUT, Dir_MEMORY;
  wire [31:0] INPUT, MEMORY_IN, MEMORY_OUT;

  Button button_1 (.out(button_1_out));
  Clock clock_1 (.out(CLK));
  D_Flip_Flop d_ff_1 (.clk(CLK), .D(1'b1), .Q(d_ff_1_q), .reset(button_1_out));  // open: Qn, preset, en
  D_Flip_Flop d_ff_2 (.clk(CLK), .D(d_ff_1_q), .Qn(CLR), .reset(button_1_out));  // open: Q, preset, en
  BIG_ASM big_asm_1 (
    .DATA_INPUT(INPUT), .MEMORY_IN(MEMORY_OUT), .CLK(CLK), .CLR(CLR), .DIR_INPUT(Dir_INPUT),
    .MEMORY_OUT(MEMORY_IN), .DIR_MEMORY(Dir_MEMORY), .Write_OUTPUT(Write), .ASCII(ASCII),
    .Write_ASCII(Write_ASCII), .END(out_1));
  MEMORY memory_1 (.DIR(Dir_MEMORY), .DATA_IN(MEMORY_IN), .WRITE(Write), .CLK(CLK), .CLR(CLR), .DATA_OUT(MEMORY_OUT));
  INPUT input_1 (.DIR(Dir_INPUT), .CLK(CLK), .DATA_OUT(INPUT));
  Counter counter_1 (.load(1'b0), .count(not_1_out), .Q(counter_1_q), .clk(CLK), .clr(CLR));  // open: D, carry
  not not_1 (not_1_out, out_1);
  // Probe on INPUT
  // Probe on counter_1_q
  TTY #(.rows(32), .cols(60)) tty_1 (.data(ASCII), .clk(CLK), .we(Write_ASCII), .clr(CLR));

  // Other names for the same wires on the sheet: END = out_1

  // Notes on the sheet:
  //   COUNTER
  //   BOARD
endmodule

module INPUT (
  input  [23:0] DIR,
  input  CLK,
  output [31:0] DATA_OUT
);

  RAM #(.addrWidth(24), .dataWidth(32)) ram_1 (.addr(DIR), .data(DATA_OUT), .clk(CLK), .ld(1'b1));  // open: sel, clr
endmodule

module MEMORY (
  input  [23:0] DIR,
  input  [31:0] DATA_IN,
  input  WRITE,
  input  CLK,
  input  CLR,
  output [31:0] DATA_OUT
);

  wire not_1_out;

  not not_1 (not_1_out, WRITE);
  RAM #(.addrWidth(24), .dataWidth(32), .bus("separate")) ram_1 (
    .addr(DIR), .din(DATA_IN), .data(DATA_OUT), .clk(CLK), .ld(not_1_out), .clr(CLR));  // open: str, sel
endmodule

module BIG_ASM (
  input  [31:0] DATA_INPUT,
  input  [31:0] MEMORY_IN,
  input  CLK,
  input  CLR,
  output [23:0] DIR_INPUT,
  output [31:0] MEMORY_OUT,
  output [23:0] DIR_MEMORY,
  output Write_OUTPUT,
  output [6:0] ASCII,
  output Write_ASCII,
  output END
);

  wire d_ff_1_q, d_ff_3_q, d_ff_5_q, demultiplexer_1_out0, demultiplexer_2_out0, demultiplexer_3_out0,
       demultiplexer_3_out1, done_print, en, en_0, en_1, IDLE_2_q, IDLE_q, or_1_out, or_2_out, or_3_out,
       reset, start, write;
  wire [6:0] print_dec_1_ascii;
  wire [31:0] multiplexer_2_out, number, X___Y, Z;

  D_Flip_Flop d_ff_1 (.clk(CLK), .D(1'b1), .Q(d_ff_1_q), .reset(CLR));  // open: Qn, preset, en
  D_Flip_Flop IDLE (.clk(CLK), .D(demultiplexer_1_out0), .Q(IDLE_q), .preset(CLR));  // open: Qn, en, reset
  Demultiplexer #(.enable("false")) demultiplexer_1 (.out0(demultiplexer_1_out0), .out1(en_0), .in(IDLE_q), .sel(END));
  D_Flip_Flop d_ff_2 (.clk(CLK), .D(d_ff_1_q), .Qn(start), .reset(CLR));  // open: Q, preset, en
  or or_1 (or_1_out, demultiplexer_2_out0, en_0);
  D_Flip_Flop IDLE_2 (.clk(CLK), .D(END), .Q(IDLE_2_q), .reset(CLR));  // open: Qn, preset, en
  Demultiplexer #(.enable("false")) demultiplexer_2 (
    .out0(demultiplexer_2_out0), .out1(en_1), .in(d_ff_3_q), .sel(done_print));
  D_Flip_Flop d_ff_3 (.clk(CLK), .D(or_1_out), .Q(d_ff_3_q), .reset(CLR));  // open: Qn, preset, en
  Resta_Fracciones resta_fracciones_1 (
    .\input (DATA_INPUT), .Clock(CLK), .Clear(CLR), .Start(start), .X___Y(X___Y), .Z(Z), .Done(END),
    .PC(DIR_INPUT));
  or or_2 (or_2_out, CLR, reset);
  // Probe on X___Y
  // Probe on Z
  PRINT_DEC print_dec_1 (
    .num(number), .start(IDLE_2_q), .CLK(CLK), .RST(or_2_out), .ASCII(print_dec_1_ascii),
    .Write_ASCII(write), .END(done_print));
  D_Flip_Flop d_ff_4 (.clk(CLK), .D(en_1), .Q(reset), .reset(CLR));  // open: Qn, preset, en
  or or_3 (or_3_out, demultiplexer_3_out0, reset);
  Multiplexer #(.width(7), .enable("false")) multiplexer_1 (
    .in0(print_dec_1_ascii), .in1(7'b0001010), .out(ASCII), .sel(en_1));
  Demultiplexer #(.enable("false")) demultiplexer_3 (
    .out0(demultiplexer_3_out0), .out1(demultiplexer_3_out1), .in(d_ff_5_q), .sel(done_print));
  D_Flip_Flop d_ff_5 (.clk(CLK), .D(or_3_out), .Q(d_ff_5_q), .reset(CLR));  // open: Qn, preset, en
  D_Flip_Flop d_ff_6 (.clk(CLK), .D(demultiplexer_3_out1), .reset(CLR));  // open: Q, Qn, preset, en
  or or_4 (en, en_0, en_1);
  Multiplexer #(.width(32), .enable("false")) multiplexer_2 (.in0(X___Y), .in1(Z), .out(multiplexer_2_out), .sel(en_1));
  or or_5 (Write_ASCII, en_1, write);
  Register #(.width(32)) register_1 (.D(multiplexer_2_out), .en(en), .Q(number), .clk(CLK), .clr(CLR));
  // Probe on number

  // Other names for the same wires on the sheet: select = en_1; select_ASCII = en_1; w0 = en_1
endmodule

module PRINT_UDEC (
  input  [31:0] num,
  input  start,
  input  CLK,
  input  RST,
  output [6:0] ASCII,
  output Write_ASCII,
  output End
);

  wire _0_c, _0_n, demultiplexer_1_out0, demultiplexer_2_out0, demultiplexer_2_out1, demultiplexer_3_out0,
       demultiplexer_3_out1, demultiplexer_4_out1, IDLE_2_q, IDLE_3_q, IDLE_4_q, IDLE_5_q, IDLE_q, Lc, Lc_0,
       Ln, Ln_0, or_1_out, or_4_out;
  wire [23:0] bit_extender_1_out;
  wire [31:0] c, c___1, c___1_t, divider_1_rem, memory_1_data_out, multiplexer_1_out, multiplexer_2_out,
       multiplexer_3_out, n, n___10, n___10___48;

  Multiplexer #(.width(32), .enable("false")) multiplexer_1 (
    .in0(num), .in1(n___10), .out(multiplexer_1_out), .sel(Lc_0));
  Divider #(.width(32)) divider_1 (.a(n), .b(32'ha), .out(n___10), .rem(divider_1_rem));  // open: upper
  Adder #(.width(32)) adder_1 (.a(divider_1_rem), .b(32'h30), .out(n___10___48));  // open: cin, cout
  or or_1 (or_1_out, demultiplexer_1_out0, demultiplexer_4_out1);
  Register #(.width(32)) u_n (.D(multiplexer_1_out), .en(Ln), .Q(n), .clk(CLK), .clr(RST));
  D_Flip_Flop IDLE (.clk(CLK), .D(or_1_out), .Q(IDLE_q), .preset(RST));  // open: Qn, en, reset
  Demultiplexer #(.enable("false")) demultiplexer_1 (
    .out0(demultiplexer_1_out0), .out1(Ln_0), .in(IDLE_q), .sel(start));
  or or_2 (Write_ASCII, demultiplexer_3_out0, demultiplexer_2_out1);
  Multiplexer #(.width(32), .enable("false")) multiplexer_2 (
    .in0(c___1), .in1(c___1_t), .out(multiplexer_2_out), .sel(Write_ASCII));
  Adder #(.width(32)) adder_2 (.a(c), .b(32'h1), .out(c___1));  // open: cin, cout
  Subtractor #(.width(32)) subtractor_1 (.a(c), .b(32'h1), .out(c___1_t));  // open: bin, bout
  D_Flip_Flop IDLE_2 (.clk(CLK), .D(Ln_0), .Q(IDLE_2_q), .reset(RST));  // open: Qn, preset, en
  Register #(.width(32)) u_c (.D(multiplexer_2_out), .en(Lc), .Q(c), .clk(CLK), .clr(RST));
  or or_3 (Lc_0, IDLE_2_q, demultiplexer_3_out1);
  Multiplexer #(.width(32), .enable("false")) multiplexer_3 (
    .in0(c), .in1(c___1_t), .out(multiplexer_3_out), .sel(Write_ASCII));
  Comparator #(.width(32), .mode("unsigned")) comparator_1 (.a({32{1'b0}}), .b(n), .lt(_0_n));  // open: gt, eq
  Comparator #(.width(32), .mode("unsigned")) comparator_2 (.a({32{1'b0}}), .b(c), .lt(_0_c));  // open: gt, eq
  D_Flip_Flop IDLE_3 (.clk(CLK), .D(Write_ASCII), .Q(IDLE_3_q), .reset(RST));  // open: Qn, preset, en
  Demultiplexer #(.enable("false")) demultiplexer_2 (
    .out0(demultiplexer_2_out0), .out1(demultiplexer_2_out1), .in(IDLE_3_q), .sel(_0_c));
  Bit_Extender #(.in_width(32), .out_width(24)) bit_extender_1 (.in(multiplexer_3_out), .out(bit_extender_1_out));
  D_Flip_Flop IDLE_4 (.clk(CLK), .D(Lc_0), .Q(IDLE_4_q), .reset(RST));  // open: Qn, preset, en
  or or_4 (or_4_out, End, demultiplexer_2_out0);
  or or_5 (Lc, Lc_0, Write_ASCII);
  or or_6 (Ln, Ln_0, Lc_0);
  Demultiplexer #(.enable("false")) demultiplexer_3 (
    .out0(demultiplexer_3_out0), .out1(demultiplexer_3_out1), .in(IDLE_4_q), .sel(_0_n));
  D_Flip_Flop IDLE_5 (.clk(CLK), .D(or_4_out), .Q(IDLE_5_q), .reset(RST));  // open: Qn, preset, en
  MEMORY memory_1 (
    .DIR(bit_extender_1_out), .DATA_IN(n___10___48), .WRITE(Lc_0), .CLK(CLK), .CLR(RST),
    .DATA_OUT(memory_1_data_out));
  Demultiplexer #(.enable("false")) demultiplexer_4 (
    .out0(End), .out1(demultiplexer_4_out1), .in(IDLE_5_q), .sel(start));
  Bit_Extender #(.in_width(32), .out_width(7)) bit_extender_2 (.in(memory_1_data_out), .out(ASCII));

  // Other names for the same wires on the sheet: Lc_1 = Write_ASCII; Sc = Write_ASCII; Ln_1 = Lc_0; Sn = Lc_0;
  //   Write = Lc_0
endmodule

module PRINT_DEC (
  input  [31:0] num,
  input  start,
  input  CLK,
  input  RST,
  output [6:0] ASCII,
  output Write_ASCII,
  output END
);

  wire demultiplexer_1_out0, demultiplexer_1_out1, demultiplexer_2_out0, demultiplexer_3_out0,
       demultiplexer_3_out1, END_q, end_t, IDLE_3_q, IDLE_q, or_1_out, or_2_out, or_4_out, S_ASCII,
       startUDEC, Write_ASCII_1;
  wire [6:0] ASCII_t;
  wire [31:0] multiplexer_1_out, negator_1_out;

  // Probe on num
  Negator #(.width(32)) negator_1 (.in(num), .out(negator_1_out));
  D_Flip_Flop IDLE (.clk(CLK), .D(demultiplexer_1_out0), .Q(IDLE_q), .preset(RST));  // open: Qn, en, reset
  Demultiplexer #(.enable("false")) demultiplexer_1 (
    .out0(demultiplexer_1_out0), .out1(demultiplexer_1_out1), .in(IDLE_q), .sel(start));
  Multiplexer #(.width(32), .enable("false")) multiplexer_1 (
    .in0(num), .in1(negator_1_out), .out(multiplexer_1_out), .sel(num[31]));
  Demultiplexer #(.enable("false")) demultiplexer_2 (
    .out0(demultiplexer_2_out0), .out1(S_ASCII), .in(demultiplexer_1_out1), .sel(num[31]));
  or or_1 (or_1_out, demultiplexer_2_out0, S_ASCII);
  D_Flip_Flop IDLE_2 (.clk(CLK), .D(or_1_out), .Q(startUDEC), .reset(RST));  // open: Qn, preset, en
  PRINT_UDEC print_udec_1 (
    .num(multiplexer_1_out), .start(startUDEC), .CLK(CLK), .RST(RST), .ASCII(ASCII_t),
    .Write_ASCII(Write_ASCII_1), .End(end_t));
  D_Flip_Flop IDLE_3 (.clk(CLK), .D(or_2_out), .Q(IDLE_3_q), .reset(RST));  // open: Qn, preset, en
  or or_2 (or_2_out, startUDEC, demultiplexer_3_out0);
  Demultiplexer #(.enable("false")) demultiplexer_3 (
    .out0(demultiplexer_3_out0), .out1(demultiplexer_3_out1), .in(IDLE_3_q), .sel(end_t));
  Multiplexer #(.width(7), .enable("false")) multiplexer_2 (
    .in0(ASCII_t), .in1(7'b0101101), .out(ASCII), .sel(S_ASCII));
  or or_3 (Write_ASCII, S_ASCII, Write_ASCII_1);
  or or_4 (or_4_out, END, demultiplexer_3_out1);
  D_Flip_Flop u_END (.clk(CLK), .D(or_4_out), .Q(END_q), .reset(RST));  // open: Qn, preset, en
  Demultiplexer #(.enable("false")) demultiplexer_4 (.out1(END), .in(END_q), .sel(end_t));  // open: out0

  // Other names for the same wires on the sheet: sign = num[31]; Write_ASCII_0 = S_ASCII
endmodule

module TEST_PRINT (
  input  [31:0] in_1,
  output out_2
);

  wire button_1_out, button_2_out, CLK, CLR, d_ff_1_q, Write_ASCII;
  wire [6:0] ASCII;

  Button button_1 (.out(button_1_out));
  Clock clock_1 (.out(CLK));
  D_Flip_Flop d_ff_1 (.clk(CLK), .D(1'b1), .Q(d_ff_1_q), .reset(button_1_out));  // open: Qn, preset, en
  D_Flip_Flop d_ff_2 (.clk(CLK), .D(d_ff_1_q), .Qn(CLR), .reset(button_1_out));  // open: Q, preset, en
  Button button_2 (.out(button_2_out));
  PRINT_UDEC print_udec_1 ();  // open: num, start, CLK, RST, ASCII, Write_ASCII, End
  PRINT_DEC print_dec_1 (
    .num(in_1), .start(button_2_out), .CLK(CLK), .RST(CLR), .ASCII(ASCII), .Write_ASCII(Write_ASCII),
    .END(out_2));
  TTY #(.rows(32), .cols(60)) tty_1 (.data(ASCII), .clk(CLK), .we(Write_ASCII), .clr(CLR));
endmodule

module MCD (
  input  [31:0] A,
  input  [31:0] B,
  input  Clock,
  input  Clear,
  input  Start,
  output [31:0] MCD,
  output Done
);

  wire A____B, A___B, mcd_control_unit_1_l_a, mcd_control_unit_1_l_b, mcd_control_unit_1_s_a;
  wire [1:0] mcd_control_unit_1_s_b;

  // Probe on A
  // Probe on B
  MCD_Control_Unit mcd_control_unit_1 (
    .A____B(A____B), .A___B(A___B), .Start(Start), .Clear(Clear), .Clock(Clock), .Done(Done),
    .L_A(mcd_control_unit_1_l_a), .L_B(mcd_control_unit_1_l_b), .S_A(mcd_control_unit_1_s_a),
    .S_B(mcd_control_unit_1_s_b));
  MCD_Data_Path mcd_data_path_1 (
    .a(A), .b(B), .L_A(mcd_control_unit_1_l_a), .L_B(mcd_control_unit_1_l_b), .S_A(mcd_control_unit_1_s_a),
    .S_B(mcd_control_unit_1_s_b), .Clock(Clock), .A___B(A___B), .A____B(A____B), .MCD(MCD), .Clear(Clear));
  // Probe on MCD

  // Other names for the same wires on the sheet: clk = Clock; clr = Clear

  // Notes on the sheet:
  //   Inputs
  //   Outputs
endmodule

// Data Path
module MCD_Data_Path (
  input  [31:0] a,
  input  [31:0] b,
  input  L_A,
  input  L_B,
  input  S_A,
  input  [1:0] S_B,
  input  Clock,
  input  Clear,
  output A___B,
  output A____B,
  output [31:0] MCD
);

  wire comparator_1_eq;
  wire [31:0] B___A, B_t, multiplexer_1_out, multiplexer_2_out;

  Comparator #(.width(32)) comparator_1 (.a(MCD), .b(B_t), .gt(A___B), .eq(comparator_1_eq));  // open: lt
  not not_1 (A____B, comparator_1_eq);
  Subtractor #(.width(32)) subtractor_1 (.a(B_t), .b(MCD), .out(B___A));  // open: bin, bout
  Multiplexer #(.width(32), .enable("false")) multiplexer_1 (.in0(a), .in1(B_t), .out(multiplexer_1_out), .sel(S_A));
  Register #(.width(32)) u_A (.D(multiplexer_1_out), .en(L_A), .Q(MCD), .clk(Clock), .clr(Clear));
  Register #(.width(32)) u_B (.D(multiplexer_2_out), .en(L_B), .Q(B_t), .clk(Clock), .clr(Clear));
  Multiplexer #(.select(2), .width(32), .enable("false")) multiplexer_2 (
    .in0(b), .in1(MCD), .in2(B___A), .out(multiplexer_2_out), .sel(S_B));  // open: in3

  // Other names for the same wires on the sheet: A_t[31:0] = MCD; Clk = Clock; Clr = Clear

  // Notes on the sheet:
  //   Inputs
  //   ALU
  //   Register File
  //   Outputs
endmodule

// Control Unit
module MCD_Control_Unit (
  input  A____B,
  input  A___B,
  input  Start,
  input  Clear,
  input  Clock,
  output Done,
  output L_A,
  output L_B,
  output S_A,
  output [1:0] S_B
);

  wire d_ff_1_q, demultiplexer_1_out0, demultiplexer_2_out0, demultiplexer_2_out1, demultiplexer_3_out0,
       demultiplexer_4_out1, END_q, IDLE_q, L_A0, or_1_out, or_2_out, or_5_out, or_6_out;

  or or_1 (or_1_out, demultiplexer_1_out0, demultiplexer_4_out1);
  D_Flip_Flop IDLE (.clk(Clock), .D(or_1_out), .Q(IDLE_q), .preset(Clear));  // open: Qn, en, reset
  Demultiplexer #(.enable("false")) demultiplexer_1 (
    .out0(demultiplexer_1_out0), .out1(L_A0), .in(IDLE_q), .sel(Start));
  or or_2 (or_2_out, L_A0, S_B[1]);
  D_Flip_Flop d_ff_1 (.clk(Clock), .D(or_2_out), .Q(d_ff_1_q), .reset(Clear));  // open: Qn, preset, en
  Demultiplexer #(.enable("false")) demultiplexer_2 (
    .out0(demultiplexer_2_out0), .out1(demultiplexer_2_out1), .in(d_ff_1_q), .sel(A____B));
  or or_3 (L_A, L_A0, S_A);
  or or_4 (L_B, L_A0, S_A, S_B[1]);
  Demultiplexer #(.enable("false")) demultiplexer_3 (
    .out0(demultiplexer_3_out0), .out1(S_A), .in(demultiplexer_2_out1), .sel(A___B));
  or or_5 (or_5_out, demultiplexer_3_out0, S_A);
  D_Flip_Flop d_ff_2 (.clk(Clock), .D(or_5_out), .Q(S_B[1]), .reset(Clear));  // open: Qn, preset, en
  or or_6 (or_6_out, Done, demultiplexer_2_out0);
  D_Flip_Flop END (.clk(Clock), .D(or_6_out), .Q(END_q), .reset(Clear));  // open: Qn, preset, en
  Demultiplexer #(.enable("false")) demultiplexer_4 (.out0(Done), .out1(demultiplexer_4_out1), .in(END_q), .sel(Start));

  assign S_B[0] = S_A;

  // Other names for the same wires on the sheet: clk = Clock; clr = Clear; L_B0 = L_A0; L_A1 = S_A; L_B1 = S_A;
  //   S_B0 = S_A; L_B2 = S_B[1]

  // Notes on the sheet:
  //   Inputs
  //   Control Unit
  //   Outputs
endmodule

// Restar \nFracciones
module Resta_Fracciones (
  input  [31:0] \input ,
  input  Clock,
  input  Clear,
  input  Start,
  output [31:0] X___Y,
  output [31:0] Z,
  output Done,
  output [23:0] PC
);

  wire done_MCD, resta_fracciones_control_unit_1_l_a, resta_fracciones_control_unit_1_l_b,
       resta_fracciones_control_unit_1_l_c, resta_fracciones_control_unit_1_l_d,
       resta_fracciones_control_unit_1_l_mcm, resta_fracciones_control_unit_1_l_pc,
       resta_fracciones_control_unit_1_s_a, resta_fracciones_control_unit_1_s_b,
       resta_fracciones_control_unit_1_s_c, resta_fracciones_control_unit_1_s_mcm,
       resta_fracciones_control_unit_1_s_pc, resta_fracciones_control_unit_1_start_mcd;

  // Probe on \input 
  Resta_Fracciones_Control_Unit resta_fracciones_control_unit_1 (
    .Start(Start), .Clock(Clock), .Clear(Clear), .L_A(resta_fracciones_control_unit_1_l_a),
    .L_B(resta_fracciones_control_unit_1_l_b), .L_C(resta_fracciones_control_unit_1_l_c),
    .L_D(resta_fracciones_control_unit_1_l_d), .L_MCM(resta_fracciones_control_unit_1_l_mcm),
    .S_A(resta_fracciones_control_unit_1_s_a), .S_B(resta_fracciones_control_unit_1_s_b),
    .S_C(resta_fracciones_control_unit_1_s_c), .Done_2(Done), .Done(done_MCD),
    .S_MCM(resta_fracciones_control_unit_1_s_mcm), .start_MCD(resta_fracciones_control_unit_1_start_mcd),
    .L_PC(resta_fracciones_control_unit_1_l_pc), .S_PC(resta_fracciones_control_unit_1_s_pc));
  Resta_Fracciones_Data_Path resta_fracciones_data_path_1 (
    .\input (\input ), .L_A(resta_fracciones_control_unit_1_l_a), .L_B(resta_fracciones_control_unit_1_l_b),
    .L_C(resta_fracciones_control_unit_1_l_c), .L_D(resta_fracciones_control_unit_1_l_d),
    .L_MCM(resta_fracciones_control_unit_1_l_mcm), .S_A(resta_fracciones_control_unit_1_s_a),
    .S_B(resta_fracciones_control_unit_1_s_b), .S_C(resta_fracciones_control_unit_1_s_c), .Clock(Clock),
    .Clear(Clear), .X___Y(X___Y), .Z(Z), .done(done_MCD), .S_MCM(resta_fracciones_control_unit_1_s_mcm),
    .start_MCD(resta_fracciones_control_unit_1_start_mcd), .L_PC(resta_fracciones_control_unit_1_l_pc),
    .S_PC(resta_fracciones_control_unit_1_s_pc), .PC(PC));
  // Probe on X___Y
  // Probe on Z

  // Other names for the same wires on the sheet: clk = Clock; clr = Clear
endmodule

// Data Path
module Resta_Fracciones_Data_Path (
  input  [31:0] \input ,
  input  L_A,
  input  L_B,
  input  Clock,
  input  L_C,
  input  Clear,
  input  L_D,
  input  L_MCM,
  input  S_A,
  input  S_B,
  input  S_C,
  input  S_MCM,
  input  start_MCD,
  input  L_PC,
  input  S_PC,
  output [31:0] X___Y,
  output [31:0] Z,
  output done,
  output [23:0] PC
);

  wire [23:0] multiplexer_5_out, PC___1;
  wire [31:0] A, A___C, B___D, B__D, C, D, MCM___B, MCM___B___A, MCM___D, MCM___D___C, MCM_B__D,
       multiplexer_1_out, multiplexer_2_out, multiplexer_3_out, multiplexer_4_out;

  Multiplier #(.width(32)) multiplier_1 (.a(X___Y), .b(D), .out(B___D));  // open: cin, cout
  MCD mcd_1 (.A(X___Y), .B(D), .MCD(B__D), .Done(done), .Clock(Clock), .Clear(Clear), .Start(start_MCD));
  Divider #(.width(32)) divider_1 (.a(Z), .b(X___Y), .out(MCM___B));  // open: upper, rem
  Divider #(.width(32)) divider_2 (.a(Z), .b(D), .out(MCM___D));  // open: upper, rem
  Subtractor #(.width(32)) subtractor_1 (.a(A), .b(C), .out(A___C));  // open: bin, bout
  Adder #(.width(24)) adder_1 (.a(PC), .b(24'h1), .out(PC___1));  // open: cin, cout
  Divider #(.width(32)) divider_3 (.a(B___D), .b(B__D), .out(MCM_B__D));  // open: upper, rem
  Multiplier #(.width(32)) multiplier_2 (.a(MCM___B), .b(A), .out(MCM___B___A));  // open: cin, cout
  Multiplier #(.width(32)) multiplier_3 (.a(MCM___D), .b(C), .out(MCM___D___C));  // open: cin, cout
  Multiplexer #(.width(32), .enable("false")) multiplexer_1 (
    .in0(\input ), .in1(MCM___B___A), .out(multiplexer_1_out), .sel(S_A));
  Multiplexer #(.width(32), .enable("false")) multiplexer_2 (
    .in0(\input ), .in1(A___C), .out(multiplexer_2_out), .sel(S_B));
  Multiplexer #(.width(32), .enable("false")) multiplexer_3 (
    .in0(\input ), .in1(MCM___D___C), .out(multiplexer_3_out), .sel(S_C));
  Multiplexer #(.width(32), .enable("false")) multiplexer_4 (
    .in0(B__D), .in1(MCM_B__D), .out(multiplexer_4_out), .sel(S_MCM));
  Multiplexer #(.width(24), .enable("false")) multiplexer_5 (
    .in0(PC), .in1(PC___1), .out(multiplexer_5_out), .sel(S_PC));
  Register #(.width(32)) u_A (.D(multiplexer_1_out), .en(L_A), .Q(A), .clk(Clock), .clr(Clear));
  Register #(.width(32)) B (.D(multiplexer_2_out), .en(L_B), .Q(X___Y), .clk(Clock), .clr(Clear));
  Register #(.width(32)) u_C (.D(multiplexer_3_out), .en(L_C), .Q(C), .clk(Clock), .clr(Clear));
  Register #(.width(32)) u_D (.D(\input ), .en(L_D), .Q(D), .clk(Clock), .clr(Clear));
  Register #(.width(32)) MCM (.D(multiplexer_4_out), .en(L_MCM), .Q(Z), .clk(Clock), .clr(Clear));
  Register #(.width(24)) u_PC (.D(multiplexer_5_out), .en(L_PC), .Q(PC), .clk(Clock), .clr(Clear));

  // Other names for the same wires on the sheet: B[31:0] = X___Y; Clk = Clock; Clr = Clear; MCM[31:0] = Z

  // Notes on the sheet:
  //   Inputs
  //   ALU
  //   Register File
  //   Outputs
endmodule

// Control Unit
module Resta_Fracciones_Control_Unit (
  input  Start,
  input  Clock,
  input  Clear,
  input  Done,
  output S_A,
  output L_A,
  output L_PC,
  output S_B,
  output L_B,
  output S_PC,
  output S_C,
  output L_C,
  output S_MCM,
  output L_D,
  output start_MCD,
  output L_MCM,
  output Done_2
);

  wire d_ff_5_q, demultiplexer_1_out0, demultiplexer_2_out0, demultiplexer_3_out1, END_q, IDLE_q, L_A0, L_B0,
       L_C0, or_1_out, or_7_out, or_9_out;

  or or_1 (or_1_out, demultiplexer_1_out0, demultiplexer_3_out1);
  Demultiplexer #(.enable("false")) demultiplexer_1 (
    .out0(demultiplexer_1_out0), .out1(L_A0), .in(IDLE_q), .sel(Start));
  D_Flip_Flop IDLE (.clk(Clock), .D(or_1_out), .Q(IDLE_q), .preset(Clear));  // open: Qn, en, reset
  D_Flip_Flop d_ff_1 (.clk(Clock), .D(L_A0), .Q(L_B0), .reset(Clear));  // open: Qn, preset, en
  or or_2 (L_A, L_A0, S_A);
  or or_3 (L_PC, L_A0, L_B0, L_C0);
  D_Flip_Flop d_ff_2 (.clk(Clock), .D(L_B0), .Q(L_C0), .reset(Clear));  // open: Qn, preset, en
  or or_4 (L_B, L_B0, S_B);
  or or_5 (S_PC, L_A0, L_B0, L_C0);
  D_Flip_Flop d_ff_3 (.clk(Clock), .D(L_C0), .Q(L_D), .reset(Clear));  // open: Qn, preset, en
  or or_6 (L_C, L_C0, S_A);
  D_Flip_Flop d_ff_4 (.clk(Clock), .D(L_D), .Q(start_MCD), .reset(Clear));  // open: Qn, preset, en
  D_Flip_Flop d_ff_5 (.clk(Clock), .D(or_7_out), .Q(d_ff_5_q), .reset(Clear));  // open: Qn, preset, en
  or or_7 (or_7_out, demultiplexer_2_out0, start_MCD);
  or or_8 (L_MCM, start_MCD, S_MCM);
  Demultiplexer #(.enable("false")) demultiplexer_2 (
    .out0(demultiplexer_2_out0), .out1(S_MCM), .in(d_ff_5_q), .sel(Done));
  D_Flip_Flop d_ff_6 (.clk(Clock), .D(S_MCM), .Q(S_A), .reset(Clear));  // open: Qn, preset, en
  D_Flip_Flop d_ff_7 (.clk(Clock), .D(S_A), .Q(S_B), .reset(Clear));  // open: Qn, preset, en
  or or_9 (or_9_out, Done_2, S_B);
  Demultiplexer #(.enable("false")) demultiplexer_3 (
    .out0(Done_2), .out1(demultiplexer_3_out1), .in(END_q), .sel(Start));
  D_Flip_Flop END (.clk(Clock), .D(or_9_out), .Q(END_q), .reset(Clear));  // open: Qn, preset, en

  assign S_C = S_A;

  // Other names for the same wires on the sheet: clk = Clock; clr = Clear; Done_MCD = Done; done_t = Done_2;
  //   L_B1 = S_B; L_A1 = S_A; L_C1 = S_A; L_MCM0 = start_MCD; L_MCM1 = S_MCM; L_PC0 = L_A0; S_PC0 = L_A0;
  //   L_PC1 = L_B0; S_PC1 = L_B0; L_PC2 = L_C0; S_PC2 = L_C0

  // Notes on the sheet:
  //   Inputs
  //   Outputs
endmodule
